# Fritzing sketch robot-avec-l293d (saved by Fritzing 0.9.3b)
breadboards: 1

parts:
  Composant1 = Arduino Nano (Rev3.0)
  VCC1 = Battery block 9V
  IC1 = L293D [package=THT]
  M1 = DC Motor
  M2 = DC Motor
  R2 = Photocell (LDR) [package=THT]
  R3 = Resistor [tolerance=±5% resistance=10k package="1206 [SMD]"]
  R4 = Resistor [tolerance=±5% resistance=10k package="1206 [SMD]"]
  R7 = Photocell (LDR) [package=THT]

nets:
  N1: Composant1.GND, VCC1.-, IC1.0V, R3.Pin_0, R4.Pin_0
  N2: Composant1.D2, IC1.In_4
  N3: Composant1.D3, IC1.In_3
  N4: Composant1.D4, IC1.In_2
  N5: Composant1.D5, IC1.In_1
  N6: Composant1.VIN, VCC1.+
  N7: Composant1.5V, IC1.Enable_1, IC1.+Vmotor, IC1.Enable_2, IC1.+V, R2.pin_1, R7.pin_1
  N8: Composant1.A1, R4.Pin_1, R7.pin_0
  N9: Composant1.A0, R2.pin_0, R3.Pin_1
  N10: IC1.Out_1_(_Controlled_by_Enable_1_), M1.pin_2
  N11: IC1.Out_2_(_Controlled_by_Enable_1_), M1.pin_1
  N12: IC1.Out_3_(_Controlled_by_Enable_2_), M2.pin_2
  N13: IC1.Out_4_(_Controlled_by_Enable_2_), M2.pin_1
